# Fritzing sketch Metronome_Scheme (saved by Fritzing 0.9.3b)

parts:
  Часть1 = Arduino Nano (Rev3.0)
  RE1 = KY-040 Rotary encoder [package=THT]
  U1 = AUDIO-JACK2 [package=audio-jack-3.5mm-smd]
  OLED1 = OLED Mono 0.56 inch blue or white
  BATT1 = LiPoly Battery (1300mAh)
  M1 = TP4056 Module [part_number=HW-107]
  S1 = Toggle Switch [package=THT]
  M2 = MT3608 Module
  S2 = Pushbutton [package="[THT]"]
  R1 = Resistor [tolerance=±5% resistance=220 package=THT]
  C1 = Ceramic Capacitor [capacitance=100nF package="200 mil [THT, multilayer]"]

nets:
  GND: Часть1.GND, RE1.GND, U1.TIP, OLED1.GND, M2.pin4, S2.Pin_3, S2.Pin_4
  N1: Часть1.D3, S2.Pin_1, S2.Pin_2
  N2: Часть1.D4, RE1.CLK
  N3: Часть1.D5, RE1.DT
  N4: Часть1.D6, RE1.SW
  N5: Часть1.D10, R1.Pin_0
  N6: Часть1.VIN, M2.pin3
  VCC: Часть1.5V, RE1.Vcc, OLED1.VCC
  N7: Часть1.A5, OLED1.SCL
  N8: Часть1.A4, OLED1.SDA
  N9: U1.TSH, C1.1
  N10: BATT1.positive, M1.BAT+
  N11: BATT1.negative, M1.BAT-
  N12: M1.OUT-#1, M2.pin1
  N13: M1.OUT-#4, S1.COM
  N14: S1.L1, M2.pin2
  N15: R1.Pin_1, C1.0

notes:
  На 3 пине педаль, обычная кнопка.
  Резистор от 400 Ом, Конденсатор 220 нФ

custom parts:
  KY-040 Rotary encoder: KY-040 Rotary Encoder with switch on breakout borad from AZ Delivery
  OLED Mono 0.56 inch blue or white: OLED, I2C 3.3V - 5V Blue and White text versions
  LiPoly Battery (1300mAh): Lithium Ion Polymer Battery (1300mAh)
  TP4056 Module: TP4056 Lithium Battery Charge Management Module Links: TP4056 website
  MT3608 Module: MT3608 Boost Converter Module Links: Aerosemi MT3608 2A Step Up Converter datasheet
